// Logisim project hw2.circ as structural Verilog: 1 circuit, main circuit main
module main (
  input  Clock
);

  wire button_1_out, comparator_1_lt, decoder_1_out1, decoder_1_out2, decoder_1_out3;
  wire [1:0] multiplexer_1_out, rom_1_data, rom_1_data_3;
  wire [5:2] rom_1_data_2;
  wire [7:0] adder_1_out, adder_2_out, multiplexer_2_out, multiplexer_3_out, multiplexer_4_out,
       multiplexer_5_out, register_1_q, register_2_q, register_3_q, register_4_q, rom_1_data_4,
       subtractor_1_out;

  Multiplexer #(.width(2), .enable("false")) multiplexer_1 (
    .in0(2'b00), .in1(rom_1_data_3), .out(multiplexer_1_out), .sel(comparator_1_lt));
  // Probe on adder_1_out
  Multiplexer #(.select(2), .width(8), .enable("false")) multiplexer_2 (
    .in0(adder_1_out), .in1(adder_1_out), .in2(adder_1_out), .in3(rom_1_data_4), .out(multiplexer_2_out),
    .sel(multiplexer_1_out));
  Button button_1 (.out(button_1_out));
  Decoder #(.select(2), .disabled(0)) decoder_1 (
    .out1(decoder_1_out1), .out2(decoder_1_out2), .out3(decoder_1_out3), .sel(rom_1_data), .en(Clock));  // open: out0
  Register #(.trigger("falling")) register_1 (
    .D(multiplexer_2_out), .Q(register_1_q), .clk(Clock), .clr(button_1_out));  // open: en
  LED led_1 (.in(button_1_out));
  // Probe on register_1_q
  // Probe on rom_1_data
  Adder adder_1 (.a(8'h1), .b(register_1_q), .out(adder_1_out));  // open: cin, cout
  Register register_2 (.D(multiplexer_5_out), .Q(register_2_q), .clk(decoder_1_out1), .clr(button_1_out));  // open: en
  Register register_3 (.D(multiplexer_5_out), .Q(register_3_q), .clk(decoder_1_out2), .clr(button_1_out));  // open: en
  Register register_4 (.D(multiplexer_5_out), .Q(register_4_q), .clk(decoder_1_out3), .clr(button_1_out));  // open: en
  // Probe on {rom_1_data_4, rom_1_data_3, rom_1_data_2, rom_1_data}
  // Probe on multiplexer_3_out
  Multiplexer #(.select(2), .width(8), .enable("false")) multiplexer_3 (
    .in0(rom_1_data_4), .in1(register_2_q), .in2(register_3_q), .in3(register_4_q), .out(multiplexer_3_out),
    .sel(rom_1_data_2[5:4]));
  // Probe on rom_1_data_2[5:4]
  // Probe on rom_1_data_2[3:2]
  Multiplexer #(.select(2), .width(8), .enable("false")) multiplexer_4 (
    .in0(rom_1_data_4), .in1(register_2_q), .in2(register_3_q), .in3(register_4_q), .out(multiplexer_4_out),
    .sel(rom_1_data_2[3:2]));
  // Probe on multiplexer_4_out
  Bit_Extender #(.in_width(1), .out_width(2)) bit_extender_1 ();  // open: in, out
  ROM #(.dataWidth(16)) rom_1 (
    .addr(register_1_q), .data({rom_1_data_4, rom_1_data_3, rom_1_data_2, rom_1_data}));  // open: sel
  // Probe on rom_1_data_4
  Adder adder_2 (.a(multiplexer_3_out), .b(multiplexer_4_out), .out(adder_2_out));  // open: cin, cout
  Subtractor subtractor_1 (.a(multiplexer_4_out), .b(multiplexer_3_out), .out(subtractor_1_out));  // open: bin, bout
  Comparator comparator_1 (.a(multiplexer_3_out), .b(multiplexer_4_out), .lt(comparator_1_lt));  // open: gt, eq
  // Probe on rom_1_data_3
  Multiplexer #(.select(2), .width(8), .enable("false")) multiplexer_5 (
    .in0(rom_1_data_4), .in1(adder_2_out), .in2(subtractor_1_out), .out(multiplexer_5_out), .sel(rom_1_data_3));  // open: in3
  // Probe on multiplexer_5_out

  // Notes on the sheet:
  //   Op
  //   Cmp
  //   Const
  //   RESET
  //   Program Counter
  //   Output Select
  //   Output Reg
  //   r0
  //   r1
  //   r2
  //   Stored Program
  //   Loaded Instruction
  //   Input Reg 2
  //   Input Reg 1
  //   contents of rom_1 (hex, n*v repeats v):
  //   0 1 2 3 4 5 6 7 8 9 a
  //   Operation
  //   Constant
  //   Arithmetic
  //   Output Bus
endmodule
